# Fritzing sketch Jar_Temperature_Detector_and_Cooling_Fan (saved by Fritzing 0.9.3b)
breadboards: 2

parts:
  DS1 = DS18B20 1-Wire Temperature Sensor [part_number=DS18B20]
  M1 = Keyes l9110 Fan module [package=THT]
  Part1 = Arduino Nano (Rev3.0) (ICSP)
  R1 = Resistor [tolerance=±5% resistance=220 package=THT]
  R2 = Resistor [tolerance=±5% resistance=220 package=THT]
  J1 = Piezo Speaker

nets:
  GND: DS1.GND, M1.pin3, Part1.GND, R1.Pin_0
  N1: DS1.DQ, Part1.D2, R2.Pin_1
  VDD: DS1.VDD, M1.pin4, Part1.5V, R2.Pin_0, J1.pin2
  N2: M1.pin1, Part1.D3
  N3: M1.pin2, Part1.D4
  N4: Part1.A0, R1.Pin_1, J1.pin1

notes:
  L9110 Fan Motor
  DS18B20 Waterproof Sensor
  Piezo Disk Sensor

custom parts:
  Keyes l9110 Fan module: Keyes l9110 Fan module. Done from pictures without an actual board to hand so breadboard may not be fully accurate.
